// Logisim project cpu.circ as structural Verilog: 6 circuits, main circuit main
module main (
  input  RESET
);

  wire AddresRel_out, and_1_out, and_2_out, and_3_out, and_4_out, and_5_out, and_6_out, and_7_out, and_8_out,
       and_9_out, clock_1_out, CycleEnd_qn, decoder_1_out0, decoder_1_out1, decoder_1_out2, decoder_1_out9,
       decoder_1_out10, decoder_1_out14, decoder_1_out15, decoder_2_out0, decoder_2_out1, decoder_2_out2,
       decoder_2_out9, decoder_2_out10, decoder_2_out14, decoder_2_out15, decoder_3_out0, decoder_3_out1,
       decoder_3_out2, decoder_3_out9, decoder_3_out10, decoder_3_out14, decoder_3_out15, instrdecoder_1_add,
       instrdecoder_1_bitnand, instrdecoder_1_call, instrdecoder_1_carryen, instrdecoder_1_cmp,
       instrdecoder_1_imm, instrdecoder_1_immsmall, instrdecoder_1_jmp, instrdecoder_1_jmpcarry,
       instrdecoder_1_jmpneg, instrdecoder_1_jmpover, instrdecoder_1_jmpzero, instrdecoder_1_load,
       instrdecoder_1_loadrel, instrdecoder_1_pop, instrdecoder_1_push, instrdecoder_1_ret,
       instrdecoder_1_stop, instrdecoder_1_store, instrdecoder_1_storerel, instrdecoder_1_sub,
       instrlendec_1_len1, instrlendec_1_len2, instrlendec_1_len3, MemRead_out, MemWrite_out, nand_1_out,
       nand_2_out, nand_3_out, nand_4_out, nand_5_out, nand_6_out, nand_7_out, nand_8_out, nor_1_out,
       nor_2_out, nor_3_out, not_1_out, not_2_out, not_3_out, not_4_out, not_5_out, not_6_out, not_7_out,
       or_1_out, or_2_out, or_3_out, or_4_out, or_5_out, or_6_out, or_7_out, or_8_out, or_9_out, StackOp_out,
       toverwrite_1_q, toverwrite_2_q, toverwrite_3_q, toverwrite_4_q;
  wire [3:0] alu_1_zero, FLAGS_q, pull_resistor_4_node;
  wire [7:0] ADDR_q, alu_1_result, BANK_q, BP_q, controlled_buffer_2_out, IR0_q, IR1_q, IR2_q,
       multiplexer_1_out, multiplexer_2_out, multiplexer_3_out, pull_resistor_3_node, ram_1_dout, RegA_q,
       RegB_q, RegC_q, rom_1_data, SP_q;
  wire [15:0] pc_1_q, pull_resistor_1_node;

  Clock clock_1 (.out(clock_1_out));
  and and_1 (and_1_out, nand_3_out, clock_1_out);
  nand nand_1 (nand_1_out, not_2_out, nand_2_out);
  nand nand_2 (nand_2_out, nand_6_out, and_2_out);
  Decoder #(.select(4)) decoder_1 (
    .out0(decoder_1_out0), .out1(decoder_1_out1), .out2(decoder_1_out2), .out9(decoder_1_out9),
    .out10(decoder_1_out10), .out14(decoder_1_out14), .out15(decoder_1_out15), .sel(IR0_q[3:0]),
    .en(nor_1_out));  // open: out3, out4, out5, out6, out7, out8, out11, out12, out13
  nor nor_1 (nor_1_out, nor_3_out, not_1_out);
  not not_1 (not_1_out, or_8_out);
  not not_2 (not_2_out, RESET);
  Pull_Resistor pull_resistor_1 (.node(pull_resistor_1_node));
  assign pull_resistor_1_node = not_2_out ? {IR1_q, IR2_q} : 16'bz;  // Controlled_Buffer controlled_buffer_1
  nor nor_2 (nor_2_out, and_1_out, CycleEnd_qn);
  assign controlled_buffer_2_out = or_4_out ? IR1_q : 8'bz;  // Controlled_Buffer controlled_buffer_2
  Pull_Resistor pull_resistor_2 (.node(controlled_buffer_2_out));
  Pull_Resistor pull_resistor_3 (.node(pull_resistor_3_node));
  nor nor_3 (nor_3_out, instrdecoder_1_bitnand, instrdecoder_1_add, instrdecoder_1_sub, instrdecoder_1_imm, instrdecoder_1_immsmall, instrdecoder_1_pop, instrdecoder_1_load, instrdecoder_1_loadrel);
  PC pc_1 (.Addr(pull_resistor_1_node), .Overwrite(nand_1_out), .CLK(or_3_out), .Q(pc_1_q));
  T_Flip_Flop CycleEnd (.T(or_8_out), .clk(and_1_out), .Qn(CycleEnd_qn), .reset(or_1_out));  // open: Q, preset
  or or_1 (or_1_out, RESET, or_2_out);
  Decoder #(.select(4)) decoder_2 (
    .out0(decoder_2_out0), .out1(decoder_2_out1), .out2(decoder_2_out2), .out9(decoder_2_out9),
    .out10(decoder_2_out10), .out14(decoder_2_out14), .out15(decoder_2_out15), .sel(IR1_q[7:4]),
    .en(not_5_out));  // open: out3, out4, out5, out6, out7, out8, out11, out12, out13
  Pull_Resistor pull_resistor_4 (.node(pull_resistor_4_node));
  assign pull_resistor_3_node = instrdecoder_1_immsmall ? {pull_resistor_4_node, IR1_q[3:0]} : 8'bz;  // Controlled_Buffer controlled_buffer_3
  and and_2 (and_2_out, and_1_out, or_8_out);
  or or_2 (or_2_out, nor_2_out, RESET);
  Register RegA (.D(multiplexer_1_out), .en(decoder_1_out0), .clk(and_1_out), .Q(RegA_q), .clr(RESET));
  nand nand_3 (nand_3_out, instrdecoder_1_stop, not_4_out);
  not not_3 (not_3_out, or_8_out);
  and and_3 (and_3_out, not_3_out, and_1_out);
  or or_3 (or_3_out, and_4_out, and_6_out, and_8_out);
  assign controlled_buffer_2_out = decoder_2_out0 ? RegA_q : 8'bz;  // Controlled_Buffer controlled_buffer_4
  assign pull_resistor_3_node = decoder_3_out0 ? RegA_q : 8'bz;  // Controlled_Buffer controlled_buffer_5
  ROM #(.addrWidth(16)) rom_1 (.addr(pc_1_q), .data(rom_1_data));
  not not_4 (not_4_out, toverwrite_1_q);
  Decoder #(.select(4)) decoder_3 (
    .out0(decoder_3_out0), .out1(decoder_3_out1), .out2(decoder_3_out2), .out9(decoder_3_out9),
    .out10(decoder_3_out10), .out14(decoder_3_out14), .out15(decoder_3_out15), .sel(IR1_q[3:0]),
    .en(not_6_out));  // open: out3, out4, out5, out6, out7, out8, out11, out12, out13
  Register RegB (.D(multiplexer_1_out), .en(decoder_1_out1), .clk(and_1_out), .Q(RegB_q), .clr(RESET));
  InstrLenDec instrlendec_1 (
    .Instr(IR0_q), .Len3(instrlendec_1_len3), .Len2(instrlendec_1_len2), .Len1(instrlendec_1_len1));
  TOverwrite toverwrite_1 (
    .D(1'b1), .Overwrite(or_2_out), .TEnable(toverwrite_1_q), .CLK(and_3_out), .Q(toverwrite_1_q));
  and and_4 (and_4_out, and_3_out, toverwrite_1_q);
  assign controlled_buffer_2_out = decoder_2_out1 ? RegB_q : 8'bz;  // Controlled_Buffer controlled_buffer_6
  assign pull_resistor_3_node = decoder_3_out1 ? RegB_q : 8'bz;  // Controlled_Buffer controlled_buffer_7
  or or_4 (or_4_out, instrdecoder_1_storerel, instrdecoder_1_imm);
  Register RegC (.D(multiplexer_1_out), .en(decoder_1_out2), .clk(and_1_out), .Q(RegC_q), .clr(RESET));
  and and_5 (and_5_out, instrlendec_1_len1, toverwrite_2_q);
  or or_5 (or_5_out, toverwrite_2_q, toverwrite_1_q);
  not not_5 (not_5_out, instrdecoder_1_imm);
  not not_6 (not_6_out, instrdecoder_1_immsmall);
  assign controlled_buffer_2_out = decoder_2_out2 ? RegC_q : 8'bz;  // Controlled_Buffer controlled_buffer_8
  assign pull_resistor_3_node = decoder_3_out2 ? RegC_q : 8'bz;  // Controlled_Buffer controlled_buffer_9
  TOverwrite toverwrite_2 (.Overwrite(or_2_out), .TEnable(or_5_out), .CLK(and_3_out), .Q(toverwrite_2_q));  // open: D
  and and_6 (and_6_out, and_3_out, toverwrite_2_q);
  Register SP (.D(multiplexer_1_out), .en(decoder_1_out9), .clk(and_1_out), .Q(SP_q), .clr(RESET));
  and and_7 (and_7_out, instrlendec_1_len2, toverwrite_3_q);
  or or_6 (or_6_out, toverwrite_3_q, toverwrite_2_q);
  TOverwrite toverwrite_3 (.Overwrite(or_2_out), .TEnable(or_6_out), .CLK(and_3_out), .Q(toverwrite_3_q));  // open: D
  and and_8 (and_8_out, and_3_out, toverwrite_3_q);
  assign controlled_buffer_2_out = decoder_2_out9 ? SP_q : 8'bz;  // Controlled_Buffer controlled_buffer_10
  assign pull_resistor_3_node = decoder_3_out9 ? SP_q : 8'bz;  // Controlled_Buffer controlled_buffer_11
  Register BP (.D(multiplexer_1_out), .en(decoder_1_out10), .clk(and_1_out), .Q(BP_q), .clr(RESET));
  and and_9 (and_9_out, instrlendec_1_len3, toverwrite_4_q);
  TOverwrite toverwrite_4 (
    .Overwrite(or_2_out), .TEnable(toverwrite_3_q), .CLK(and_3_out), .Q(toverwrite_4_q));  // open: D
  or or_7 (or_7_out, decoder_3_out10, instrdecoder_1_storerel);
  assign controlled_buffer_2_out = decoder_2_out10 ? BP_q : 8'bz;  // Controlled_Buffer controlled_buffer_12
  assign pull_resistor_3_node = or_7_out ? BP_q : 8'bz;  // Controlled_Buffer controlled_buffer_13
  Register IR0 (.D(rom_1_data), .en(toverwrite_1_q), .clk(or_3_out), .Q(IR0_q), .clr(RESET));
  or or_8 (or_8_out, and_5_out, and_7_out, and_9_out);
  Register BANK (.D(multiplexer_1_out), .en(decoder_1_out14), .clk(and_1_out), .Q(BANK_q), .clr(RESET));
  assign controlled_buffer_2_out = decoder_2_out14 ? BANK_q : 8'bz;  // Controlled_Buffer controlled_buffer_14
  assign pull_resistor_3_node = decoder_3_out14 ? BANK_q : 8'bz;  // Controlled_Buffer controlled_buffer_15
  Register IR1 (.D(rom_1_data), .en(toverwrite_2_q), .clk(or_3_out), .Q(IR1_q), .clr(RESET));
  Register ADDR (.D(multiplexer_1_out), .en(decoder_1_out15), .clk(and_1_out), .Q(ADDR_q), .clr(RESET));
  assign controlled_buffer_2_out = decoder_2_out15 ? ADDR_q : 8'bz;  // Controlled_Buffer controlled_buffer_16
  assign pull_resistor_3_node = decoder_3_out15 ? ADDR_q : 8'bz;  // Controlled_Buffer controlled_buffer_17
  or or_9 (or_9_out, instrdecoder_1_cmp, instrdecoder_1_sub);
  Register IR2 (.D(rom_1_data), .en(toverwrite_3_q), .clk(or_3_out), .Q(IR2_q), .clr(RESET));
  or MemRead (MemRead_out, instrdecoder_1_loadrel, instrdecoder_1_load);
  or MemWrite (MemWrite_out, instrdecoder_1_storerel, instrdecoder_1_store);
  nand nand_4 (nand_4_out, FLAGS_q[2], instrdecoder_1_jmpover);
  nand nand_5 (nand_5_out, FLAGS_q[0], instrdecoder_1_jmpzero);
  Register #(.width(4)) FLAGS (.D(alu_1_zero), .en(nor_1_out), .clk(and_1_out), .Q(FLAGS_q), .clr(RESET));
  or AddresRel (AddresRel_out, instrdecoder_1_storerel, instrdecoder_1_loadrel);
  Multiplexer #(.width(8)) multiplexer_1 (
    .in0(alu_1_result), .in1(ram_1_dout), .out(multiplexer_1_out), .sel(MemRead_out));
  or StackOp (StackOp_out, instrdecoder_1_push, instrdecoder_1_ret, instrdecoder_1_call, instrdecoder_1_pop);
  nand nand_6 (nand_6_out, nand_4_out, nand_7_out, nand_5_out, nand_8_out, not_7_out);
  nand nand_7 (nand_7_out, FLAGS_q[3], instrdecoder_1_jmpneg);
  nand nand_8 (nand_8_out, FLAGS_q[1], instrdecoder_1_jmpcarry);
  ALU alu_1 (
    .Passthrough(instrdecoder_1_imm), .CarryFlag(FLAGS_q[1]), .CarryEn(instrdecoder_1_carryen),
    .A(controlled_buffer_2_out), .B(pull_resistor_3_node), .Subtract(or_9_out),
    .BitNAND(instrdecoder_1_bitnand), .Result(alu_1_result), .Zero(alu_1_zero[0]), .CarryOut(alu_1_zero[1]),
    .Overflow(alu_1_zero[2]), .Negative(alu_1_zero[3]));
  InstrDecoder instrdecoder_1 (
    .Instr(IR0_q), .Stop(instrdecoder_1_stop), .Add(instrdecoder_1_add), .Sub(instrdecoder_1_sub),
    .CarryEn(instrdecoder_1_carryen), .BitNAND(instrdecoder_1_bitnand), .Cmp(instrdecoder_1_cmp),
    .ImmSmall(instrdecoder_1_immsmall), .Imm(instrdecoder_1_imm), .Jmp(instrdecoder_1_jmp),
    .JmpZero(instrdecoder_1_jmpzero), .JmpNeg(instrdecoder_1_jmpneg), .JmpCarry(instrdecoder_1_jmpcarry),
    .JmpOver(instrdecoder_1_jmpover), .Push(instrdecoder_1_push), .Pop(instrdecoder_1_pop),
    .Ret(instrdecoder_1_ret), .Call(instrdecoder_1_call), .StoreRel(instrdecoder_1_storerel),
    .LoadRel(instrdecoder_1_loadrel), .Store(instrdecoder_1_store), .Load(instrdecoder_1_load));
  not not_7 (not_7_out, instrdecoder_1_jmp);
  Multiplexer #(.width(8)) multiplexer_2 (
    .in0(ADDR_q), .in1(alu_1_result), .out(multiplexer_2_out), .sel(AddresRel_out));
  Multiplexer #(.width(8)) multiplexer_3 (.in0(BANK_q), .in1({8{1'b1}}), .out(multiplexer_3_out), .sel(StackOp_out));
  RAM #(.addrWidth(16)) ram_1 (
    .addr({multiplexer_3_out, multiplexer_2_out}), .we(MemWrite_out), .oe(MemRead_out), .clk(or_8_out),
    .din(alu_1_result), .dout(ram_1_dout));

  // Notes on the sheet:
  //   contents of rom_1 (hex, n*v repeats v):
  //   a0 0 ae 0 af 0 60 1 6f 0 30 e0 0 6
endmodule

module ALU (
  input  Passthrough,
  input  CarryFlag,
  input  CarryEn,
  input  [7:0] A,
  input  [7:0] B,
  input  Subtract,
  input  BitNAND,
  output [7:0] Result,
  output Zero,
  output CarryOut,
  output Overflow,
  output Negative
);

  wire and_1_out, nor_1_out, nor_6_out, nor_11_out, nor_12_out, nor_13_out, nor_14_out, nor_15_out,
       nor_16_out, nor_17_out, not_1_out, not_2_out, not_3_out, not_4_out, not_5_out, not_6_out, not_7_out,
       not_8_out, not_9_out, not_10_out, xor_1_out, xor_2_out, xor_3_out, xor_4_out, xor_5_out, xor_6_out,
       xor_7_out, xor_8_out;
  wire [6:0] adder_1_out;
  wire [7:0] nand_1_out, nor_2_out;

  not not_1 (not_1_out, BitNAND);
  nor nor_1 (nor_1_out, not_1_out, Passthrough);
  xor xor_1 (xor_1_out, B[0], Subtract);
  xor xor_2 (xor_2_out, B[1], Subtract);
  xor xor_3 (xor_3_out, B[2], Subtract);
  xor xor_4 (xor_4_out, B[3], Subtract);
  not not_2 (not_2_out, xor_1_out);
  not not_3 (not_3_out, xor_2_out);
  not not_4 (not_4_out, xor_3_out);
  not not_5 (not_5_out, xor_4_out);
  nor nor_2 (nor_2_out[0], not_2_out, Passthrough);
  nor nor_3 (nor_2_out[1], not_3_out, Passthrough);
  nor nor_4 (nor_2_out[2], not_4_out, Passthrough);
  nor nor_5 (nor_2_out[3], not_5_out, Passthrough);
  nand nand_1 (nand_1_out[0], A[0], B[0]);
  nand nand_2 (nand_1_out[1], A[1], B[1]);
  nand nand_3 (nand_1_out[2], A[2], B[2]);
  nand nand_4 (nand_1_out[3], A[3], B[3]);
  not not_6 (not_6_out, Subtract);
  xor xor_5 (xor_5_out, B[4], Subtract);
  not not_7 (not_7_out, xor_5_out);
  xor xor_6 (xor_6_out, B[5], Subtract);
  not not_8 (not_8_out, xor_6_out);
  xor xor_7 (xor_7_out, B[6], Subtract);
  not not_9 (not_9_out, xor_7_out);
  xor xor_8 (xor_8_out, B[7], Subtract);
  not not_10 (not_10_out, xor_8_out);
  nand nand_5 (nand_1_out[4], A[4], B[4]);
  nand nand_6 (nand_1_out[5], A[5], B[5]);
  nand nand_7 (nand_1_out[6], A[6], B[6]);
  nand nand_8 (nand_1_out[7], A[7], B[7]);
  and and_1 (and_1_out, CarryFlag, CarryEn);
  nor nor_6 (nor_6_out, CarryEn, not_6_out);
  nor nor_7 (nor_2_out[4], not_7_out, Passthrough);
  nor nor_8 (nor_2_out[5], not_8_out, Passthrough);
  nor nor_9 (nor_2_out[6], not_9_out, Passthrough);
  nor nor_10 (nor_2_out[7], not_10_out, Passthrough);
  nor nor_11 (nor_11_out, and_1_out, nor_6_out);
  nor nor_12 (nor_12_out, nor_11_out, Passthrough);
  Adder adder_1 (.a(A), .b(nor_2_out), .out({Negative, adder_1_out}), .cin(nor_12_out), .cout(CarryOut));
  nor nor_13 (nor_13_out, A[7], B[7]);
  Multiplexer #(.width(8)) multiplexer_1 (
    .in0({Negative, adder_1_out}), .in1(nand_1_out), .out(Result), .sel(nor_1_out));
  nor nor_14 (nor_14_out, Result[0], Result[1]);
  nor nor_15 (nor_15_out, Result[4], Result[5]);
  and and_2 (Overflow, Negative, nor_13_out);
  nor nor_16 (nor_16_out, Result[2], Result[3]);
  nor nor_17 (nor_17_out, Result[6], Result[7]);
  and and_3 (Zero, nor_14_out, nor_15_out, nor_16_out, nor_17_out);
endmodule

module TOverwrite (
  input  D,
  input  Overwrite,
  input  TEnable,
  input  CLK,
  output Q
);

  wire and_1_out, and_2_out, nand_1_out, nand_2_out, nand_3_out, nand_4_out, nand_5_out, nand_6_out,
       nor_1_out, nor_3_out, not_1_out, not_2_out, not_3_out, not_4_out, not_5_out;

  not not_1 (not_1_out, CLK);
  not not_2 (not_2_out, not_1_out);
  not not_3 (not_3_out, not_2_out);
  not not_4 (not_4_out, Overwrite);
  and and_1 (and_1_out, TEnable, nor_1_out);
  nor nor_1 (nor_1_out, CLK, not_3_out);
  and and_2 (and_2_out, and_1_out, not_4_out);
  nand nand_1 (nand_1_out, Q, and_2_out);
  nand nand_2 (nand_2_out, and_2_out, nor_3_out);
  not not_5 (not_5_out, D);
  nand nand_3 (nand_3_out, not_5_out, Overwrite);
  nand nand_4 (nand_4_out, D, Overwrite);
  nand nand_5 (nand_5_out, nand_1_out, nand_3_out);
  nand nand_6 (nand_6_out, nand_4_out, nand_2_out);
  nor nor_2 (Q, nand_5_out, nor_3_out);
  nor nor_3 (nor_3_out, Q, nand_6_out);
endmodule

module PC (
  input  [15:0] Addr,
  input  Overwrite,
  input  CLK,
  output [15:0] Q
);

  TOverwrite toverwrite_1 (.D(Addr[0]), .Overwrite(Overwrite), .TEnable(1'b1), .CLK(CLK), .Q(Q[0]));
  TOverwrite toverwrite_2 (.D(Addr[8]), .Overwrite(Overwrite), .TEnable(1'b1), .CLK(Q[7]), .Q(Q[8]));
  TOverwrite toverwrite_3 (.D(Addr[1]), .Overwrite(Overwrite), .TEnable(1'b1), .CLK(Q[0]), .Q(Q[1]));
  TOverwrite toverwrite_4 (.D(Addr[9]), .Overwrite(Overwrite), .TEnable(1'b1), .CLK(Q[8]), .Q(Q[9]));
  TOverwrite toverwrite_5 (.D(Addr[2]), .Overwrite(Overwrite), .TEnable(1'b1), .CLK(Q[1]), .Q(Q[2]));
  TOverwrite toverwrite_6 (.D(Addr[10]), .Overwrite(Overwrite), .TEnable(1'b1), .CLK(Q[9]), .Q(Q[10]));
  TOverwrite toverwrite_7 (.D(Addr[3]), .Overwrite(Overwrite), .TEnable(1'b1), .CLK(Q[2]), .Q(Q[3]));
  TOverwrite toverwrite_8 (.D(Addr[11]), .Overwrite(Overwrite), .TEnable(1'b1), .CLK(Q[10]), .Q(Q[11]));
  TOverwrite toverwrite_9 (.D(Addr[4]), .Overwrite(Overwrite), .TEnable(1'b1), .CLK(Q[3]), .Q(Q[4]));
  TOverwrite toverwrite_10 (.D(Addr[12]), .Overwrite(Overwrite), .TEnable(1'b1), .CLK(Q[11]), .Q(Q[12]));
  TOverwrite toverwrite_11 (.D(Addr[5]), .Overwrite(Overwrite), .TEnable(1'b1), .CLK(Q[4]), .Q(Q[5]));
  TOverwrite toverwrite_12 (.D(Addr[13]), .Overwrite(Overwrite), .TEnable(1'b1), .CLK(Q[12]), .Q(Q[13]));
  TOverwrite toverwrite_13 (.D(Addr[6]), .Overwrite(Overwrite), .TEnable(1'b1), .CLK(Q[5]), .Q(Q[6]));
  TOverwrite toverwrite_14 (.D(Addr[14]), .Overwrite(Overwrite), .TEnable(1'b1), .CLK(Q[13]), .Q(Q[14]));
  TOverwrite toverwrite_15 (.D(Addr[7]), .Overwrite(Overwrite), .TEnable(1'b1), .CLK(Q[6]), .Q(Q[7]));
  TOverwrite toverwrite_16 (.D(Addr[15]), .Overwrite(Overwrite), .TEnable(1'b1), .CLK(Q[14]), .Q(Q[15]));
endmodule

module InstrLenDec (
  input  [7:0] Instr,
  output Len3,
  output Len2,
  output Len1
);

  wire nand_1_out, nand_2_out, nand_3_out, nor_1_out, not_1_out, not_2_out;

  not not_1 (not_1_out, Len1);
  and and_1 (Len3, Instr[7], not_1_out, Instr[6]);
  nor nor_1 (nor_1_out, Instr[4], Instr[6], Instr[7]);
  not not_2 (not_2_out, Instr[5]);
  nand nand_1 (nand_1_out, nor_1_out, not_2_out);
  nand nand_2 (nand_2_out, nor_1_out, Instr[5]);
  nand nand_3 (nand_3_out, Instr[4], Instr[5], Instr[6], Instr[7]);
  nand nand_4 (Len1, nand_1_out, nand_2_out, nand_3_out);
  nor nor_2 (Len2, Len3, Len1);
endmodule

module InstrDecoder (
  input  [7:0] Instr,
  output Stop,
  output Add,
  output Sub,
  output CarryEn,
  output BitNAND,
  output Cmp,
  output ImmSmall,
  output Imm,
  output Jmp,
  output JmpZero,
  output JmpNeg,
  output JmpCarry,
  output JmpOver,
  output Push,
  output Pop,
  output Ret,
  output Call,
  output StoreRel,
  output LoadRel,
  output Store,
  output Load
);

  wire and_1_out, nand_1_out, nor_7_out, nor_8_out, nor_9_out, nor_10_out, nor_11_out, nor_12_out,
       nor_13_out, nor_17_out, not_1_out, not_2_out, not_3_out, not_4_out, not_6_out, not_7_out, or_1_out;

  nand nand_1 (nand_1_out, Instr[3], nor_17_out, Instr[1]);
  not not_1 (not_1_out, Instr[4]);
  not not_2 (not_2_out, Instr[5]);
  not not_3 (not_3_out, Instr[6]);
  not not_4 (not_4_out, Instr[7]);
  or or_1 (or_1_out, Instr[7], Instr[6], Instr[5], Instr[4]);
  not not_5 (Call, nand_1_out);
  not not_6 (not_6_out, Instr[1]);
  not not_7 (not_7_out, Instr[0]);
  nor nor_1 (Push, Instr[7], Instr[6], Instr[5], not_1_out);
  and and_1 (and_1_out, nor_17_out, nand_1_out);
  nor nor_2 (Cmp, not_6_out, or_1_out);
  nor nor_3 (Stop, Instr[0], Cmp, or_1_out);
  nor nor_4 (Ret, not_7_out, or_1_out);
  nor nor_5 (Pop, Instr[7], Instr[6], not_2_out, Instr[4]);
  nor nor_6 (Store, Instr[7], Instr[6], not_2_out, not_1_out);
  and and_2 (JmpZero, and_1_out, Instr[0]);
  and and_3 (JmpCarry, and_1_out, Instr[2]);
  nor nor_7 (nor_7_out, Instr[7], not_3_out, Instr[5], Instr[4]);
  nor nor_8 (nor_8_out, Instr[7], not_3_out, Instr[5], not_1_out);
  and and_4 (JmpNeg, and_1_out, Instr[1]);
  and and_5 (JmpOver, and_1_out, Instr[3]);
  nor nor_9 (nor_9_out, Instr[0], Instr[3], Instr[1], Instr[2]);
  nor nor_10 (nor_10_out, Instr[7], not_3_out, not_2_out, not_1_out);
  nor nor_11 (nor_11_out, Instr[7], not_3_out, not_2_out, Instr[4]);
  and and_6 (Jmp, nor_17_out, nor_9_out);
  or or_2 (Add, nor_7_out, nor_8_out, nor_11_out);
  nor nor_12 (nor_12_out, not_4_out, Instr[6], Instr[5], Instr[4]);
  nor nor_13 (nor_13_out, not_4_out, Instr[6], Instr[5], not_1_out);
  nor nor_14 (Imm, not_4_out, Instr[6], not_2_out, Instr[4]);
  or or_3 (ImmSmall, nor_13_out, nor_11_out);
  or or_4 (Sub, nor_10_out, nor_12_out, nor_13_out);
  nor nor_15 (BitNAND, not_4_out, Instr[6], not_2_out, not_1_out);
  or or_5 (CarryEn, nor_8_out, nor_12_out);
  nor nor_16 (StoreRel, not_4_out, not_3_out, Instr[5], Instr[4]);
  nor nor_17 (nor_17_out, not_4_out, not_3_out, not_2_out, Instr[4]);
  nor nor_18 (Load, not_4_out, not_3_out, not_2_out, not_1_out);
  nor nor_19 (LoadRel, not_4_out, not_3_out, Instr[5], not_1_out);
endmodule
